# Fritzing sketch PCB (saved by Fritzing 0.9.3b)
circuit board: 13.0604cm x 5.54517cm
breadboards: 1

parts:
  U1 = IC, DIP package, 14 pins [chip_label=LM324 part_number=OP-amp]
  U2 = IC, DIP package, 14 pins [chip_label=LM324 part_number=OP-amp]
  C1 = Electrolytic Capacitor [capacitance=1µF package="100 mil [THT, electrolytic]"]
  C2 = Electrolytic Capacitor [capacitance=1µF package="100 mil [THT, electrolytic]"]
  C3 = Electrolytic Capacitor [capacitance=1µF package="100 mil [THT, electrolytic]"]
  R1 = Resistor [tolerance=±5% resistance=10k package=THT]
  R2 = Resistor [tolerance=±5% resistance=10k package=THT]
  R3 = Resistor [tolerance=±5% resistance=10k package=THT]
  C4 = Ceramic Capacitor [capacitance=100nF package="100 mil [THT, multilayer]"]
  R4 = Resistor [tolerance=±5% resistance=220 package=THT]
  C5 = Ceramic Capacitor [capacitance=100nF package="100 mil [THT, multilayer]"]
  C6 = Ceramic Capacitor [capacitance=100nF package="100 mil [THT, multilayer]"]
  R6 = Resistor [tolerance=±5% resistance=220 package=THT]
  Rectifier = IC, DIP package, 4 pins [chip_label=DB107]
  R7 = Resistor [tolerance=±5% resistance=220 package=THT]
  R8 = Resistor [tolerance=±5% resistance=220 package=THT]
  R9 = Resistor [tolerance=±5% resistance=220 package=THT]
  R10 = Resistor [tolerance=±5% resistance=220 package=THT]
  C7 = Ceramic Capacitor [capacitance=100nF package="100 mil [THT, multilayer]"]
  VR1 = Voltage Regulator - 5V [package="TO220 [THT]"]
  A1 = IC, SIP package, 3 pins [chip_label=ACS712 part_number="Hall Sensor"]
  A2 = IC, SIP package, 3 pins [chip_label=ACS712 part_number="Hall Sensor"]
  A3 = IC, SIP package, 3 pins [chip_label=ACS712 part_number="Hall Sensor"]
  T1 = mystery part, 2 pins [chip_label=Transformer(230V-9V) part_number=Transformer]
  C8 = Ceramic Capacitor [capacitance=100nF package="100 mil [THT, multilayer]"]
  R11 = Resistor [tolerance=±5% resistance=220 package=THT]
  D1 = Rectifier Diode [part_number=1N4001 package="300 mil [THT]"]
  C9 = Electrolytic Capacitor [capacitance=1µF package="100 mil [THT, electrolytic]"]
  R13 = Resistor [tolerance=±5% resistance=220 package=THT]
  R14 = Resistor [tolerance=±5% resistance=220 package=THT]
  C10 = Electrolytic Capacitor [capacitance=1µF package="100 mil [THT, electrolytic]"]
  B1 = mystery part, 6 pins [chip_label="Bug Strip"]
  V2 = DC Power [voltage=12V]
  B2 = mystery part, 6 pins [chip_label="Bug Strip"]
  U3 = mystery part, 1 pin [chip_label=?]
  U5 = mystery part, 1 pin [chip_label=?]
  U6 = mystery part, 1 pin [chip_label=?]
  U7 = mystery part, 1 pin [chip_label=?]
  U8 = mystery part, 1 pin [chip_label=?]
  U9 = mystery part, 1 pin [chip_label=?]
  U10 = mystery part, 1 pin [chip_label=?]
  U11 = mystery part, 1 pin [chip_label=?]
  U12 = mystery part, 1 pin [chip_label=?]
  U13 = mystery part, 1 pin [chip_label=?]
  U14 = mystery part, 1 pin [chip_label=?]
  U15 = mystery part, 1 pin [chip_label=?]
  U17 = mystery part, 1 pin [chip_label=?]
  U18 = mystery part, 1 pin [chip_label=?]
  R5 = Resistor [tolerance=±5% resistance=220 package=THT]
  R15 = Resistor [tolerance=±5% resistance=220 package=THT]
  C11 = Ceramic Capacitor [capacitance=100nF package="100 mil [THT, multilayer]"]
  C12 = Ceramic Capacitor [capacitance=100nF package="100 mil [THT, multilayer]"]
  R16 = Resistor [tolerance=±5% resistance=220 package=THT]
  C13 = Ceramic Capacitor [capacitance=100nF package="100 mil [THT, multilayer]"]
  R17 = Resistor [tolerance=±5% resistance=220 package=THT]
  D2 = Rectifier Diode [part_number=1N4001 package="300 mil [THT]"]
  D3 = Rectifier Diode [part_number=1N4001 package="300 mil [THT]"]
  D4 = Rectifier Diode [part_number=1N4001 package="300 mil [THT]"]
  R18 = Resistor [tolerance=±5% resistance=220 package=THT]
  R19 = Resistor [tolerance=±5% resistance=220 package=THT]
  R20 = Resistor [tolerance=±5% resistance=220 package=THT]
  U19 = mystery part, 1 pin [chip_label=?]
  U20 = mystery part, 1 pin [chip_label=?]
  U21 = mystery part, 1 pin [chip_label=?]
  U22 = mystery part, 1 pin [chip_label=?]
  U23 = mystery part, 1 pin [chip_label=?]
  U24 = mystery part, 1 pin [chip_label=?]
  R12 = Resistor [tolerance=±5% resistance=220 package=THT]
  U25 = mystery part, 1 pin [chip_label=?]
  U26 = mystery part, 1 pin [chip_label=?]

nets:
  N1: U1.pin1, U1.pin2, C4.1, U3.pin1
  N2: U1.pin3, U1.pin5, C1.-, R1.Pin_0
  5V: U1.pin4, U2.pin4, VR1.output_voltage, A1.pin1, A2.pin1, A3.pin1, R14.Pin_1, C10.+, B2.pin1, B2.pin2, B2.pin3, B2.pin4, B2.pin5, B2.pin6, U12.pin1, U14.pin1
  GND: U1.pin6, U1.pin9, U1.pin11, U2.pin6, U2.pin11, U2.pin13, R1.Pin_1, R2.Pin_1, R3.Pin_1, R4.Pin_0, R6.Pin_1, Rectifier.pin3, R7.Pin_1, R8.Pin_1, R9.Pin_1, C7.0, A1.pin3, A2.pin3, A3.pin3, R11.Pin_1, C9.-, R13.Pin_0, C10.-, B1.pin1, B1.pin2, B1.pin3, B1.pin4, B1.pin5, B1.pin6, V2.V-, U7.pin1, U8.pin1, U9.pin1, R5.Pin_1, R15.Pin_1, R16.Pin_1, R17.Pin_1, R12.Pin_1
  N3: U1.pin7, C11.1
  N4: U1.pin8, C12.0
  N5: U1.pin10, U1.pin12, C2.-, R2.Pin_0, U5.pin1, U6.pin1
  N6: U1.pin13, U1.pin14, C5.0
  N7: U2.pin1, U2.pin2, C6.1
  N8: U2.pin3, U2.pin5, C3.-, R3.Pin_0, U10.pin1, U11.pin1
  N9: U2.pin7, C13.1
  N10: U2.pin12, Rectifier.pin1, R7.Pin_0, T1.pin2, U13.pin1, U15.pin1
  N11: U2.pin14, C8.0, U17.pin1, U18.pin1
  N12: C1.+, A1.pin2
  N13: C2.+, A2.pin2
  N14: C3.+, A3.pin2
  N15: C4.0, R4.Pin_1, U19.pin1
  N16: C5.1, R5.Pin_0, U23.pin1
  N17: C6.0, R6.Pin_0, U24.pin1
  N18: Rectifier.pin2, R8.Pin_0, T1.pin1
  N19: Rectifier.pin4, R10.Pin_0
  N20: R9.Pin_0, R10.Pin_1, C7.1, U26.pin1
  N21: VR1.input_voltage, C9.+, V2.V+
  N22: VR1.GND, R13.Pin_1, R14.Pin_0
  N23: C8.1, R11.Pin_0, D1.anode
  N24: D1.cathode, R12.Pin_0, U25.pin1
  N25: R15.Pin_0, C11.0, D2.anode
  N26: C12.1, R16.Pin_0, D3.anode
  N27: C13.0, R17.Pin_0, D4.anode
  N28: D2.cathode, R20.Pin_1, U20.pin1
  N29: D3.cathode, R18.Pin_1, U21.pin1
  N30: D4.cathode, R19.Pin_1, U22.pin1
  N31: R18.Pin_0, R19.Pin_0, R20.Pin_0
