# Fritzing sketch Schematic file (saved by Fritzing 0.9.3b)
breadboards: 1

parts:
  A4 = IC, SIP package, 3 pins [chip_label=ACS712 part_number="Hall Sensor"]
  A5 = IC, SIP package, 3 pins [chip_label=ACS712 part_number="Hall Sensor"]
  A6 = IC, SIP package, 3 pins [chip_label=ACS712 part_number="Hall Sensor"]
  C11 = Electrolytic Capacitor [capacitance=2.2µF package="100 mil [THT, electrolytic]"]
  C12 = Electrolytic Capacitor [capacitance=2.2µF package="100 mil [THT, electrolytic]"]
  C13 = Electrolytic Capacitor [capacitance=2.2µF package="100 mil [THT, electrolytic]"]
  C15 = Ceramic Capacitor [capacitance=10nF package="100 mil [THT, multilayer]"]
  R19 = Resistor [tolerance=±5% resistance=100k package=THT]
  R20 = Resistor [tolerance=±5% resistance=100k package=THT]
  R21 = Resistor [tolerance=±5% resistance=900k package=THT]
  R23 = Resistor [tolerance=±5% resistance=33k package=THT]
  R24 = Resistor [tolerance=±5% resistance=1M package=THT]
  R26 = Resistor [tolerance=±5% resistance=1M package=THT]
  Rectifier1 = IC, DIP package, 4 pins [chip_label=DB107]
  C17 = Ceramic Capacitor [capacitance=10nF package="100 mil [THT, multilayer]"]
  T2 = mystery part, 2 pins [chip_label=Transformer(230V-9V) part_number=Transformer]
  D2 = Rectifier Diode [part_number=1N4148 package="300 mil [THT]"]
  R27 = Resistor [tolerance=±5% resistance=10 package=THT]
  R28 = Resistor [tolerance=±5% resistance=330 package=THT]
  V4 = DC Power [voltage=12V]
  VR2 = Voltage Regulator - 5V [package="TO220 [THT]"]
  C21 = Electrolytic Capacitor [capacitance=10µF package="100 mil [THT, electrolytic]"]
  C22 = Electrolytic Capacitor [capacitance=100nF package="100 mil [THT, electrolytic]"]
  R29 = Resistor [tolerance=±5% resistance=1k package=THT]
  C23 = Ceramic Capacitor [capacitance=10nF package="100 mil [THT, multilayer]"]
  C24 = Ceramic Capacitor [capacitance=10nF package="100 mil [THT, multilayer]"]
  R30 = Resistor [tolerance=±5% resistance=100k package=THT]
  R32 = Resistor [tolerance=±5% resistance=33k package=THT]
  U21 = IC, DIP package, 14 pins [chip_label=LM324 part_number=OP-amp]
  C26 = Ceramic Capacitor [capacitance=10nF package="100 mil [THT, multilayer]"]
  C27 = Ceramic Capacitor [capacitance=10nF package="100 mil [THT, multilayer]"]
  C28 = Ceramic Capacitor [capacitance=10nF package="100 mil [THT, multilayer]"]
  C29 = Ceramic Capacitor [capacitance=10nF package="100 mil [THT, multilayer]"]
  R33 = Resistor [tolerance=±5% resistance=1k package=THT]
  R34 = Resistor [tolerance=±5% resistance=1k package=THT]
  R35 = Resistor [tolerance=±5% resistance=100k package=THT]
  R36 = Resistor [tolerance=±5% resistance=100k package=THT]
  R37 = Resistor [tolerance=±5% resistance=33k package=THT]
  R38 = Resistor [tolerance=±5% resistance=33k package=THT]
  D4 = Rectifier Diode [part_number=1N4001 package="300 mil [THT]"]
  D5 = Rectifier Diode [part_number=1N4001 package="300 mil [THT]"]
  U20 = IC, DIP package, 14 pins [chip_label=LM324 part_number=OP-amp]
  Male_header = mystery part, 10 pins [chip_label=?]
  R39 = Resistor [tolerance=±5% resistance=10k package=THT]
  R40 = Resistor [tolerance=±5% resistance=10k package=THT]
  R41 = Resistor [tolerance=±5% resistance=10k package=THT]
  D3 = Rectifier Diode [part_number=1N4148 breakdown_voltage=3.6V package="300 mil [THT]"]

nets:
  5V: A4.pin1, A5.pin1, A6.pin1, R28.Pin_1, VR2.output_voltage, C22.+, U21.pin4, U20.pin4, Male_header.pin10
  N1: A4.pin2, C13.+
  GND: A4.pin3, A5.pin3, A6.pin3, R19.Pin_1, R20.Pin_1, R23.Pin_1, R24.Pin_1, R26.Pin_1, Rectifier1.pin3, C17.0, R27.Pin_0, V4.V-, C21.-, C22.-, C23.1, R30.Pin_1, R32.Pin_1, U21.pin6, U21.pin9, U21.pin11, C27.0, C29.1, R35.Pin_1, R36.Pin_1, R37.Pin_1, R38.Pin_1, U20.pin6, U20.pin9, U20.pin11, Male_header.pin9, R39.Pin_0, R40.Pin_0, R41.Pin_0
  N2: A5.pin2, C11.+
  N3: A6.pin2, C12.+
  curr1: C11.-, U21.pin3, U21.pin5, R41.Pin_1
  curr2: C12.-, U21.pin10, U21.pin12, R40.Pin_1
  curr3: C13.-, U20.pin3, U20.pin5, R39.Pin_1
  N4: C15.0, U20.pin8
  N5: C15.1, R20.Pin_0, D2.anode
  volt_signal: R19.Pin_0, R21.Pin_1, C17.1, Male_header.pin4
  N6: R21.Pin_0, Rectifier1.pin4
  Frequency: R23.Pin_0, D2.cathode, Male_header.pin8
  volt: R24.Pin_0, Rectifier1.pin1, T2.pin2, U20.pin10
  N7: R26.Pin_0, Rectifier1.pin2, T2.pin1
  N8: R27.Pin_1, R28.Pin_0, VR2.GND
  12V: V4.V+, VR2.input_voltage, C21.+
  curr_signal3: R29.Pin_0, C23.0, Male_header.pin3
  N9: R29.Pin_1, U20.pin1, U20.pin2
  N10: C24.0, U20.pin7
  N11: C24.1, R30.Pin_0, D3.anode
  phase3: R32.Pin_0, Male_header.pin7, D3.cathode
  N12: U21.pin1, U21.pin2, R34.Pin_1
  N13: U21.pin7, C28.0
  N14: U21.pin8, C26.0
  N15: U21.pin13, U21.pin14, R33.Pin_0
  N16: C26.1, R35.Pin_0, D4.anode
  curr_signal2: C27.1, R33.Pin_1, Male_header.pin2
  N17: C28.1, R36.Pin_0, D5.anode
  curr_signal1: C29.0, R34.Pin_0, Male_header.pin1
  phase1: R37.Pin_0, D5.cathode, Male_header.pin5
  phase2: R38.Pin_0, D4.cathode, Male_header.pin6
